// Logisim project Mux 4;1.circ as structural Verilog: 1 circuit, main circuit main
module main (
  input  E0,
  input  E1,
  input  E2,
  input  E3,
  input  ctrl,
  input  ctrl_2,
  output out_7,
  output out_8,
  output out_9,
  output out_10
);

  wire not_1_out, not_2_out;

  not not_1 (not_1_out, ctrl);
  not not_2 (not_2_out, ctrl_2);
  and and_1 (out_7, E0, not_2_out, not_1_out);
  and and_2 (out_8, E1, not_1_out, ctrl_2);
  and and_3 (out_9, E2, ctrl, not_2_out);
  and and_4 (out_10, E3, ctrl, ctrl_2);
endmodule
